# Fritzing sketch AQSensor_v1 (saved by Fritzing 0.9.3b)
breadboards: 1

parts:
  U1 = NodeMCU V1.0
  Part1 = Adafruit SGP30 Gas Sensor
  Part3 = Adafruit BME280
  Part4 = Adafruit PMSA003I Air Quality Breakout [part_number="Adafruit #4632"]

nets:
  N1: U1.D1, Part1.SCL, Part3.SCK/SCL, Part4.SCL
  N2: U1.D2, Part1.SDA, Part3.SDI/SDA, Part4.SDA
  GND: U1.GND, Part1.GND, Part3.GND, Part4.GND
  VIN: U1.Vin, Part1.VIN, Part3.VIN, Part4.VCC

custom parts:
  NodeMCU V1.0: ESP8266 based NodeMCU
  Adafruit BME280: Bosch has stepped up their game with their new BME280 sensor, an environmental sensor with temperature, barometric pressure and humidity! This sensor is great for all sorts of weather/environmental sensing and can even be used in both I2C and SPI! This precision sensor from Bosch is the best low-cost sensing solution for measuring humidity with ±3% accuracy, barometric pressure with ±1 hPa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
  Adafruit PMSA003I Air Quality Breakout: Breathe easy, knowing that you can track and sense the quality of the air around you with this Adafruit PMSA003I Air Quality Breakout. This sensor is great for monitoring air quality, in a compact plug-in format. Best of all, unlike almost all other sensors we've seen that are UART interface, this one is I2C interface, which makes it a great match for single board Linux computers like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
